// Digital circuit Assignment1OzanDural2021556027.dig as structural Verilog
module Assignment1OzanDural2021556027 (
  input  A,
  input  B,
  output Y,
  output X
);

  wire and_1_out, not_1_out, xor_1_out;

  not not_1 (not_1_out, B);
  xor xor_1 (xor_1_out, A, B);
  and and_1 (and_1_out, A, not_1_out);
  nand nand_1 (X, xor_1_out, and_1_out);
  nor nor_1 (Y, xor_1_out, and_1_out);
endmodule
